// Logisim project Associação Serie Aula memória GRandão.circ as structural Verilog: 1 circuit, main circuit main
module main (
  input  [11:0] \Pos__Memória ,
  input  [7:0] Entrada,
  input  [1:0] in_3,
  input  clear,
  input  R_W,
  output [7:0] \Saída 
);

  wire CK_out, decoder_1_out0, decoder_1_out1, decoder_1_out2, decoder_1_out3;

  Clock CK (.out(CK_out));
  Decoder #(.select(2), .enable("false")) decoder_1 (
    .out0(decoder_1_out0), .out1(decoder_1_out1), .out2(decoder_1_out2), .out3(decoder_1_out3), .sel(in_3));
  RAM #(.addrWidth(12), .bus("separate")) ram_1 (
    .addr(\Pos__Memória ), .din(Entrada), .data(\Saída ), .sel(decoder_1_out0), .clk(CK_out), .ld(R_W),
    .clr(clear));  // open: str
  RAM #(.addrWidth(12), .bus("separate")) ram_2 (
    .addr(\Pos__Memória ), .din(Entrada), .data(\Saída ), .sel(decoder_1_out1), .clk(CK_out), .ld(R_W),
    .clr(clear));  // open: str
  RAM #(.addrWidth(12), .bus("separate")) ram_3 (
    .addr(\Pos__Memória ), .din(Entrada), .data(\Saída ), .sel(decoder_1_out2), .clk(CK_out), .ld(R_W),
    .clr(clear));  // open: str
  RAM #(.addrWidth(12), .bus("separate")) ram_4 (
    .addr(\Pos__Memória ), .din(Entrada), .data(\Saída ), .sel(decoder_1_out3), .clk(CK_out), .ld(R_W),
    .clr(clear));  // open: str

  // Notes on the sheet:
  //   M1
  //   m2
  //   m3
  //   m4
endmodule
