// Logisim project CONTADOR DE DÉCADA ASSINCRONO CRESCENTE.circ as structural Verilog: 1 circuit, main circuit main
module main (
  output out_1,
  output out_2,
  output out_3,
  output out_4
);

  wire clock_1_out, not_1_out, or_1_out, t_ff_2_qn, t_ff_4_qn;

  Clock clock_1 (.out(clock_1_out));
  not not_1 (not_1_out, or_1_out);
  or or_1 (or_1_out, out_4, t_ff_2_qn, out_2, t_ff_4_qn);
  T_Flip_Flop #(.trigger("falling")) t_ff_1 (
    .clk(clock_1_out), .T(1'b1), .Q(out_4), .reset(not_1_out));  // open: Qn, preset, en
  T_Flip_Flop #(.trigger("falling")) t_ff_2 (
    .clk(out_4), .T(1'b1), .Q(out_3), .Qn(t_ff_2_qn), .reset(not_1_out));  // open: preset, en
  T_Flip_Flop #(.trigger("falling")) t_ff_3 (
    .clk(out_3), .T(1'b1), .Q(out_2), .reset(not_1_out));  // open: Qn, preset, en
  T_Flip_Flop #(.trigger("falling")) t_ff_4 (
    .clk(out_2), .T(1'b1), .Q(out_1), .Qn(t_ff_4_qn), .reset(not_1_out));  // open: preset, en
endmodule
