// Logisim project CONTADOR SINCRONO HEXADECIMAL CRESCENTE.circ as structural Verilog: 1 circuit, main circuit main
module main (
  output out_1,
  output out_2,
  output out_3,
  output out_4,
  output a,
  output b,
  output c,
  output d
);

  wire and_1_out, and_2_out, and_3_out, and_4_out, and_5_out, and_6_out, and_7_out, and_8_out, and_9_out,
       clock_1_out, not_1_out, not_2_out, not_3_out, not_4_out, not_5_out, not_6_out, not_8_out, not_9_out,
       not_10_out;

  Clock clock_1 (.out(clock_1_out));
  D_Flip_Flop #(.trigger("falling")) d_ff_1 (.clk(clock_1_out), .D(a), .Q(out_1));  // open: Qn, preset, en, reset
  D_Flip_Flop #(.trigger("falling")) d_ff_2 (.clk(clock_1_out), .D(b), .Q(out_2));  // open: Qn, preset, en, reset
  D_Flip_Flop #(.trigger("falling")) d_ff_3 (.clk(clock_1_out), .D(c), .Q(out_3));  // open: Qn, preset, en, reset
  not not_1 (not_1_out, out_1);
  not not_2 (not_2_out, out_2);
  not not_3 (not_3_out, out_3);
  not not_4 (not_4_out, out_4);
  not not_5 (not_5_out, out_3);
  not not_6 (not_6_out, out_4);
  not not_7 (d, out_4);
  and and_1 (and_1_out, not_1_out, out_2, out_3, out_4);
  and and_2 (and_2_out, out_1, not_8_out);
  not not_8 (not_8_out, out_2);
  and and_3 (and_3_out, out_1, not_9_out);
  not not_9 (not_9_out, out_3);
  and and_4 (and_4_out, out_1, not_10_out);
  not not_10 (not_10_out, out_4);
  and and_5 (and_5_out, not_2_out, out_3, out_4);
  and and_6 (and_6_out, out_2, not_3_out);
  and and_7 (and_7_out, out_2, not_4_out);
  and and_8 (and_8_out, not_5_out, out_4);
  and and_9 (and_9_out, out_3, not_6_out);
  D_Flip_Flop #(.trigger("falling")) d_ff_4 (.clk(clock_1_out), .D(d), .Q(out_4));  // open: Qn, preset, en, reset
  or or_1 (a, and_1_out, and_2_out, and_3_out, and_4_out);
  or or_2 (b, and_5_out, and_6_out, and_7_out);
  or or_3 (c, and_8_out, and_9_out);
endmodule
