// Logisim project ERRO-CONTAR-ATE12.circ as structural Verilog: 1 circuit, main circuit main
module main (
  output out_1,
  output out_2,
  output out_3,
  output out_4,
  output A,
  output B,
  output C,
  output D
);

  wire and_1_out, and_2_out, and_3_out, and_4_out, and_5_out, and_6_out, clock_1_out, not_1_out, not_2_out,
       not_3_out, not_4_out, not_5_out;

  D_Flip_Flop #(.trigger("falling")) d_ff_1 (.clk(clock_1_out), .D(A), .Q(out_1));  // open: Qn, preset, en, reset
  Clock clock_1 (.out(clock_1_out));
  D_Flip_Flop #(.trigger("falling")) d_ff_2 (.clk(clock_1_out), .D(B), .Q(out_2));  // open: Qn, preset, en, reset
  and and_1 (and_1_out, out_2, out_3, out_4);
  not not_1 (not_1_out, out_2);
  not not_2 (not_2_out, out_3);
  not not_3 (not_3_out, out_4);
  not not_4 (not_4_out, out_3);
  not not_5 (not_5_out, out_4);
  not not_6 (D, out_4);
  D_Flip_Flop #(.trigger("falling")) d_ff_3 (.clk(clock_1_out), .D(C), .Q(out_3));  // open: Qn, preset, en, reset
  or or_1 (A, and_1_out, out_1);
  and and_2 (and_2_out, not_1_out, out_3, out_4);
  and and_3 (and_3_out, out_2, not_2_out);
  and and_4 (and_4_out, out_2, not_3_out);
  and and_5 (and_5_out, not_4_out, out_4);
  and and_6 (and_6_out, out_3, not_5_out);
  D_Flip_Flop #(.trigger("falling")) d_ff_4 (.clk(clock_1_out), .D(D), .Q(out_4));  // open: Qn, preset, en, reset
  or or_2 (B, and_2_out, and_3_out, and_4_out);
  or or_3 (C, and_5_out, and_6_out);
endmodule
