// Logisim project EX1-LISTA-FLIP-FLOP.circ as structural Verilog: 1 circuit, main circuit main
module main (
  input  A,
  input  B,
  output Q
);

  wire and_1_out, nand_1_out;

  and and_1 (and_1_out, B, A);
  nand nand_1 (nand_1_out, A, B);
  NotExactlyOne xnor_1 (.out(Q), .in0(nand_1_out), .in1(and_1_out), .in2(Q));
endmodule
