// Logisim project EX2-LISTA-FLIP-FLOP.circ as structural Verilog: 1 circuit, main circuit main
module main (
  input  A,
  input  B,
  output Q,
  output nQ
);

  wire clock_1_out, xnor_1_out, xor_1_out;

  Clock clock_1 (.out(clock_1_out));
  xor xor_1 (xor_1_out, A, B);
  xnor xnor_1 (xnor_1_out, A, B);
  J_K_Flip_Flop #(.trigger("falling")) j_k_ff_1 (
    .J(xor_1_out), .clk(clock_1_out), .K(xnor_1_out), .Q(Q), .Qn(nQ));  // open: preset, en, reset
endmodule
