// Logisim project EX2-LISTA5.circ as structural Verilog: 1 circuit, main circuit main
module main (
  input  [1:0] in_1,
  input  in_2,
  input  in_3,
  output out_4,
  output out_5,
  output out_6,
  output out_7,
  output out_8,
  output out_9,
  output out_10,
  output out_11
);

  wire clock_1_out;

  Clock clock_1 (.out(clock_1_out));
  Demultiplexer #(.select(2), .enable("false")) demultiplexer_1 (
    .out0(out_6), .out1(out_5), .out2(out_8), .out3(out_9), .in(1'b1), .sel(in_1));
  J_K_Flip_Flop j_k_ff_1 (.J(in_2), .clk(clock_1_out), .K(in_3), .Q(out_10), .Qn(out_11));  // open: preset, en, reset

  assign out_4 = 1'b1;
  assign out_7 = out_5;
endmodule
