// Logisim project EX3-SLIDE-FLIP-FLOP.circ as structural Verilog: 1 circuit, main circuit main
module main (
  input  A,
  output out_2,
  output out_3,
  output out_4,
  output out_5
);

  wire clock_1_out, not_1_out;

  Clock clock_1 (.out(clock_1_out));
  J_K_Flip_Flop #(.trigger("falling")) j_k_ff_1 (
    .J(A), .clk(clock_1_out), .K(A), .Q(out_2), .Qn(out_4));  // open: preset, en, reset
  not not_1 (not_1_out, out_2);
  J_K_Flip_Flop #(.trigger("falling")) j_k_ff_2 (
    .J(out_2), .clk(clock_1_out), .K(not_1_out), .Q(out_3), .Qn(out_5));  // open: preset, en, reset
endmodule
