// Logisim project EX3CODIFDEC.circ as structural Verilog: 1 circuit, main circuit main
module main (
  input  A,
  input  B,
  input  C,
  input  D,
  output S1,
  output S2,
  output S3,
  output S4
);

  wire and_1_out, and_2_out, and_3_out, and_4_out, and_5_out, and_6_out, not_1_out, not_2_out, not_3_out,
       not_4_out, not_5_out, not_6_out;

  not not_1 (not_1_out, A);
  and and_1 (and_1_out, not_1_out, B);
  and and_2 (and_2_out, A, not_2_out);
  not not_2 (not_2_out, B);
  not not_3 (not_3_out, B);
  and and_3 (and_3_out, not_3_out, C);
  and and_4 (and_4_out, B, not_4_out);
  not not_4 (not_4_out, C);
  not not_5 (not_5_out, C);
  and and_5 (and_5_out, not_5_out, D);
  and and_6 (and_6_out, C, not_6_out);
  not not_6 (not_6_out, D);
  or or_1 (S2, and_1_out, and_2_out);
  or or_2 (S3, and_3_out, and_4_out);
  or or_3 (S4, and_5_out, and_6_out);

  assign S1 = A;
endmodule
