// Logisim project EX4-LISTA-FLIP-FLOP.circ as structural Verilog: 1 circuit, main circuit main
module main (
  input  CONTROLE_ENTRADA_EVITAR_ERRO,
  input  E3,
  input  E2,
  input  E1,
  input  E0,
  input  HABILIT,
  input  CONTROLE_ENTRADA_EVITAR_ERRO_2,
  output S,
  output S3,
  output S2,
  output S1,
  output S0
);

  wire _1_2_qn, _1_q, _1_qn, _2_2_qn, _2_q, _2_qn, _3_2_qn, _3_q, _3_qn, clock_1_out, clock_2_out,
       nand_1_out, nand_2_out, nand_3_out, nand_4_out, not_1_out, not_2_out;

  not not_1 (not_1_out, CONTROLE_ENTRADA_EVITAR_ERRO);
  Clock clock_1 (.out(clock_1_out));
  not not_2 (not_2_out, CONTROLE_ENTRADA_EVITAR_ERRO_2);
  Clock clock_2 (.out(clock_2_out));
  J_K_Flip_Flop _3 (
    .J(CONTROLE_ENTRADA_EVITAR_ERRO), .clk(clock_1_out), .K(not_1_out), .Q(_3_q), .Qn(_3_qn),
    .preset(nand_1_out), .reset(HABILIT));  // open: en
  nand nand_1 (nand_1_out, E3, HABILIT);
  J_K_Flip_Flop _3_2 (
    .J(CONTROLE_ENTRADA_EVITAR_ERRO_2), .clk(clock_2_out), .K(not_2_out), .Q(S3), .Qn(_3_2_qn));  // open: preset, en, reset
  J_K_Flip_Flop _2 (
    .J(_3_q), .clk(clock_1_out), .K(_3_qn), .Q(_2_q), .Qn(_2_qn), .preset(nand_2_out), .reset(HABILIT));  // open: en
  nand nand_2 (nand_2_out, E2, HABILIT);
  J_K_Flip_Flop _2_2 (.J(S3), .clk(clock_2_out), .K(_3_2_qn), .Q(S2), .Qn(_2_2_qn));  // open: preset, en, reset
  J_K_Flip_Flop _1 (
    .J(_2_q), .clk(clock_1_out), .K(_2_qn), .Q(_1_q), .Qn(_1_qn), .preset(nand_3_out), .reset(HABILIT));  // open: en
  nand nand_3 (nand_3_out, E1, HABILIT);
  J_K_Flip_Flop _1_2 (.J(S2), .clk(clock_2_out), .K(_2_2_qn), .Q(S1), .Qn(_1_2_qn));  // open: preset, en, reset
  J_K_Flip_Flop _0 (.J(S1), .clk(clock_2_out), .K(_1_2_qn), .Q(S0));  // open: Qn, preset, en, reset
  J_K_Flip_Flop _0_2 (
    .J(_1_q), .clk(clock_1_out), .K(_1_qn), .Q(S), .preset(nand_4_out), .reset(HABILIT));  // open: Qn, en
  nand nand_4 (nand_4_out, E0, HABILIT);
endmodule
