// Logisim project EX5 P2.circ as structural Verilog: 1 circuit, main circuit main
module main (
  input  in_1,
  output QT,
  output out_3,
  output QD
);

  wire clock_1_out;

  Clock clock_1 (.out(clock_1_out));
  T_Flip_Flop #(.trigger("falling")) t_ff_1 (.clk(clock_1_out), .T(in_1), .Q(QT));  // open: Qn, preset, reset, en
  D_Flip_Flop #(.trigger("falling")) d_ff_1 (.clk(clock_1_out), .D(in_1), .Q(QD));  // open: Qn, preset, en, reset
  Multiplexer multiplexer_1 (.in0(QT), .in1(QD), .out(out_3), .sel(clock_1_out));  // open: en
endmodule
