// Logisim project EXECESSO3AULA.circ as structural Verilog: 1 circuit, main circuit main
module main (
  input  A,
  input  B,
  input  C,
  input  D,
  output S1,
  output S2,
  output S3,
  output S4
);

  wire and_1_out, and_2_out, and_3_out, and_4_out, and_5_out, and_6_out, and_7_out, not_1_out, not_2_out,
       not_3_out, not_4_out, not_5_out, not_6_out;

  and and_1 (and_1_out, B, D);
  and and_2 (and_2_out, B, C);
  not not_1 (not_1_out, B);
  and and_3 (and_3_out, not_1_out, D);
  not not_2 (not_2_out, B);
  and and_4 (and_4_out, not_2_out, C);
  not not_3 (not_3_out, C);
  and and_5 (and_5_out, B, not_3_out, not_4_out);
  not not_4 (not_4_out, D);
  not not_5 (not_5_out, C);
  and and_6 (and_6_out, not_5_out, not_6_out);
  not not_6 (not_6_out, D);
  and and_7 (and_7_out, C, D);
  not not_7 (S4, D);
  or or_1 (S1, and_1_out, and_2_out, A);
  or or_2 (S2, and_3_out, and_4_out, and_5_out);
  or or_3 (S3, and_6_out, and_7_out);
endmodule
