// Logisim project EXIMPRESSORA.circ as structural Verilog: 1 circuit, main circuit main
module main (
  input  C1,
  input  C2,
  input  C3,
  input  C4,
  input  C5,
  input  C6,
  input  C7,
  input  [2:0] TECLADO,
  input  C8,
  output IMPRESSORA
);

  Multiplexer #(.select(3), .enable("false")) multiplexer_1 (
    .in0(C1), .in1(C2), .in2(C3), .in3(C4), .in4(C5), .in5(C6), .in6(C7), .in7(C8), .out(IMPRESSORA),
    .sel(TECLADO));
endmodule
