// Logisim project FF JK MS BRUTO.circ as structural Verilog: 1 circuit, main circuit main
module main (
  input  set_J,
  input  reset_K,
  output Q,
  output nQ
);

  wire clock_1_out, nand_1_out, nand_2_out, nand_3_out, nand_4_out, nand_5_out, nand_6_out, not_1_out;

  Clock clock_1 (.out(clock_1_out));
  nand nand_1 (nand_1_out, set_J, nQ, clock_1_out);
  nand nand_2 (nand_2_out, clock_1_out, Q, reset_K);
  not not_1 (not_1_out, clock_1_out);
  nand nand_3 (nand_3_out, nand_1_out, nand_4_out);
  nand nand_4 (nand_4_out, nand_3_out, nand_2_out);
  nand nand_5 (nand_5_out, not_1_out, nand_3_out);
  nand nand_6 (nand_6_out, nand_4_out, not_1_out);
  nand nand_7 (Q, nQ, nand_5_out);
  nand nand_8 (nQ, nand_6_out, Q);
endmodule
