// Logisim project FLIP-FLOP-EX5-SLIDE.circ as structural Verilog: 1 circuit, main circuit main
module main (
  input  CK,
  input  A,
  input  B,
  output Q,
  output nQ
);

  wire xnor_1_out;

  xnor xnor_1 (xnor_1_out, A, B);
  J_K_Flip_Flop #(.trigger("falling")) j_k_ff_1 (
    .J(B), .clk(CK), .K(xnor_1_out), .Q(Q), .Qn(nQ));  // open: preset, en, reset
endmodule
