// Logisim project GEILSO FARIA RODRIGUES DA SILVA.circ as structural Verilog: 1 circuit, main circuit main
module main (
  input  D,
  output out_2,
  output out_3,
  output out_4,
  output out_5,
  output S0,
  output S1,
  output S2
);

  wire and_1_out, and_2_out, and_3_out, and_4_out, and_5_out, clock_1_out, not_1_out, not_2_out, not_3_out,
       not_4_out, not_5_out;

  Clock clock_1 (.out(clock_1_out));
  D_Flip_Flop d_ff_1 (.clk(clock_1_out), .D(S0), .Q(out_2));  // open: Qn, preset, en, reset
  not not_1 (not_1_out, out_2);
  not not_2 (not_2_out, out_3);
  not not_3 (not_3_out, out_4);
  not not_4 (not_4_out, out_3);
  not not_5 (not_5_out, out_4);
  not not_6 (S2, out_4);
  D_Flip_Flop d_ff_2 (.clk(clock_1_out), .D(S1), .Q(out_3));  // open: Qn, preset, en, reset
  and and_1 (and_1_out, not_1_out, out_3, out_4);
  and and_2 (and_2_out, out_2, not_2_out);
  and and_3 (and_3_out, out_2, not_3_out);
  and and_4 (and_4_out, not_4_out, out_4);
  and and_5 (and_5_out, out_3, not_5_out);
  D_Flip_Flop d_ff_3 (.clk(clock_1_out), .D(S2), .Q(out_4));  // open: Qn, preset, en, reset
  or or_1 (S0, and_1_out, and_2_out, and_3_out);
  or or_2 (S1, and_4_out, and_5_out);

  assign out_5 = 1'b1;
endmodule
