// Logisim project JK-SIMPLES SR.circ as structural Verilog: 1 circuit, main circuit main
module main (
  input  set_J,
  input  reset_K,
  output Q,
  output nQ
);

  wire clock_1_out, nand_1_out, nand_2_out;

  Clock clock_1 (.out(clock_1_out));
  nand nand_1 (nand_1_out, set_J, clock_1_out, nQ);
  nand nand_2 (nand_2_out, Q, clock_1_out, reset_K);
  nand nand_3 (Q, nand_1_out, nQ);
  nand nand_4 (nQ, Q, nand_2_out);
endmodule
