// Logisim project MUX16COM4.circ as structural Verilog: 1 circuit, main circuit main
module main (
  input  E0,
  input  E1,
  input  E2,
  input  E3,
  input  E4,
  input  E5,
  input  E6,
  input  E7,
  input  E8,
  input  E9,
  input  E10,
  input  E11,
  input  E12,
  input  E13,
  input  E14,
  input  E15,
  input  [1:0] in_17,
  input  [1:0] in_18,
  output S
);

  wire multiplexer_1_out, multiplexer_2_out, multiplexer_3_out, multiplexer_4_out;

  Multiplexer #(.select(2), .enable("false")) multiplexer_1 (
    .in0(E0), .in1(E1), .in2(E2), .in3(E3), .out(multiplexer_1_out), .sel(in_18));
  Multiplexer #(.select(2), .enable("false")) multiplexer_2 (
    .in0(E4), .in1(E5), .in2(E6), .in3(E7), .out(multiplexer_2_out), .sel(in_18));
  Multiplexer #(.select(2), .enable("false")) multiplexer_3 (
    .in0(E8), .in1(E9), .in2(E10), .in3(E11), .out(multiplexer_3_out), .sel(in_18));
  Multiplexer #(.select(2), .enable("false")) multiplexer_4 (
    .in0(E12), .in1(E13), .in2(E14), .in3(E15), .out(multiplexer_4_out), .sel(in_18));
  Multiplexer #(.select(2), .enable("false")) multiplexer_5 (
    .in0(multiplexer_1_out), .in1(multiplexer_2_out), .in2(multiplexer_3_out), .in3(multiplexer_4_out),
    .out(S), .sel(in_17));
endmodule
