// Logisim project Projetar um circuito contador.circ as structural Verilog: 1 circuit, main circuit main
module main (
  input  X,
  output msb,
  output lsb
);

  wire clock_1_out, t_ff_1_qn, xor_1_out;

  Clock clock_1 (.out(clock_1_out));
  T_Flip_Flop #(.trigger("falling")) t_ff_1 (
    .clk(clock_1_out), .T(1'b1), .Q(lsb), .Qn(t_ff_1_qn));  // open: preset, reset, en
  T_Flip_Flop #(.trigger("falling")) t_ff_2 (.clk(xor_1_out), .T(1'b1), .Q(msb));  // open: Qn, preset, reset, en
  xor xor_1 (xor_1_out, t_ff_1_qn, X);

  // Notes on the sheet:
  //   Usando uma variaável de controle X.X=1 crescente X=0 descrescente
  //   Projetar um circuito contador assincrono de 0 a 3 p/ operar de forma crescente decrescente
endmodule
