// Logisim project RAM PARALELA AULA.circ as structural Verilog: 1 circuit, main circuit main
module main (
  input  [9:0] in_1,
  input  [3:0] Entrada_Modulo_1,
  input  in_3,
  input  [3:0] \Entrada_Módulo_2 ,
  input  R_W,
  input  Clear,
  output [3:0] out_7,
  output [3:0] out_8
);

  wire clock_out, decoder_1_out0, decoder_1_out1;

  Decoder #(.enable("false")) decoder_1 (.out0(decoder_1_out0), .out1(decoder_1_out1), .sel(in_3));
  Clock clock (.out(clock_out));
  RAM #(.addrWidth(10), .dataWidth(4), .bus("separate")) ram_1 (
    .addr(in_1), .din(Entrada_Modulo_1), .data(out_7), .sel(decoder_1_out0), .clk(clock_out), .ld(R_W),
    .clr(Clear));  // open: str
  RAM #(.addrWidth(10), .dataWidth(4), .bus("separate")) ram_2 (
    .addr(in_1), .din(\Entrada_Módulo_2 ), .data(out_8), .sel(decoder_1_out1), .clk(clock_out), .ld(R_W),
    .clr(Clear));  // open: str

  // Notes on the sheet:
  //   Seleciona salect Módulos
  //   Módulo 1
  //   Módulo 2
endmodule
