// Logisim project REG DESLOCA P2.circ as structural Verilog: 1 circuit, main circuit main
module main (
  output Q3,
  output Q2,
  output Q1,
  output Q0,
  output out_5,
  output out_6,
  output out_7,
  output out_8
);

  wire and_1_out, and_2_out, clock_1_out, d_ff_1_qn, d_ff_4_qn, or_1_out;

  or or_1 (or_1_out, and_1_out, and_2_out);
  Clock clock_1 (.out(clock_1_out));
  and and_1 (and_1_out, out_5, out_8);
  and and_2 (and_2_out, d_ff_4_qn, d_ff_1_qn);
  D_Flip_Flop #(.trigger("falling")) d_ff_1 (
    .clk(clock_1_out), .D(or_1_out), .Q(out_8), .Qn(d_ff_1_qn));  // open: preset, en, reset
  D_Flip_Flop #(.trigger("falling")) d_ff_2 (.clk(clock_1_out), .D(out_8), .Q(out_7));  // open: Qn, preset, en, reset
  D_Flip_Flop #(.trigger("falling")) d_ff_3 (.clk(clock_1_out), .D(out_7), .Q(out_6));  // open: Qn, preset, en, reset
  D_Flip_Flop #(.trigger("falling")) d_ff_4 (
    .clk(clock_1_out), .D(out_6), .Q(out_5), .Qn(d_ff_4_qn));  // open: preset, en, reset

  assign Q0 = out_5;
  assign Q1 = out_6;
  assign Q2 = out_7;
  assign Q3 = out_8;
endmodule
