// Logisim project REG PARALELO-PARELO - PARELO -SERIE.circ as structural Verilog: 1 circuit, main circuit main
module main (
  input  in_1,
  input  MR,
  input  PL,
  input  E3,
  input  E2,
  input  E1,
  input  E0,
  output out_8,
  output out_9,
  output out_10,
  output out_11
);

  wire and_1_out, and_2_out, and_3_out, and_4_out, clock_1_out, not_1_out;

  Clock clock_1 (.out(clock_1_out));
  D_Flip_Flop d_ff_1 (.clk(clock_1_out), .D(in_1), .Q(out_8), .preset(and_1_out), .reset(not_1_out));  // open: Qn, en
  not not_1 (not_1_out, MR);
  and and_1 (and_1_out, E3, PL);
  D_Flip_Flop d_ff_2 (.clk(clock_1_out), .D(out_8), .Q(out_9), .preset(and_2_out), .reset(not_1_out));  // open: Qn, en
  and and_2 (and_2_out, E2, PL);
  D_Flip_Flop d_ff_3 (.clk(clock_1_out), .D(out_9), .Q(out_10), .preset(and_3_out), .reset(not_1_out));  // open: Qn, en
  and and_3 (and_3_out, E1, PL);
  and and_4 (and_4_out, E0, PL);
  D_Flip_Flop d_ff_4 (
    .clk(clock_1_out), .D(out_10), .Q(out_11), .preset(and_4_out), .reset(not_1_out));  // open: Qn, en
endmodule
