// Logisim project REG PARELO-PARALELO.circ as structural Verilog: 1 circuit, main circuit main
module main (
  input  E3,
  input  E2,
  input  E1,
  input  E0,
  output S3,
  output S2,
  output S1,
  output S0
);

  wire clock_1_out;

  Clock clock_1 (.out(clock_1_out));
  D_Flip_Flop d_ff_1 (.clk(clock_1_out), .D(E3), .Q(S3));  // open: Qn, preset, en, reset
  D_Flip_Flop d_ff_2 (.clk(clock_1_out), .D(E2), .Q(S2));  // open: Qn, preset, en, reset
  D_Flip_Flop d_ff_3 (.clk(clock_1_out), .D(E1), .Q(S1));  // open: Qn, preset, en, reset
  D_Flip_Flop d_ff_4 (.clk(clock_1_out), .D(E0), .Q(S0));  // open: Qn, preset, en, reset
endmodule
