// Logisim project REG TIPO D com JK MS-SERIE-PARELELO-DESLOCAMENTO.circ as structural Verilog: 1 circuit, main circuit main
module main (
  input  ES,
  output out_2,
  output out_3,
  output out_4,
  output out_5
);

  wire clock_1_out, not_1_out, not_2_out, not_3_out, not_4_out;

  Clock clock_1 (.out(clock_1_out));
  not not_1 (not_1_out, ES);
  J_K_Flip_Flop #(.trigger("falling")) j_k_ff_1 (
    .J(ES), .clk(clock_1_out), .K(not_1_out), .Q(out_2));  // open: Qn, preset, en, reset
  not not_2 (not_2_out, out_2);
  J_K_Flip_Flop #(.trigger("falling")) j_k_ff_2 (
    .J(out_2), .clk(clock_1_out), .K(not_2_out), .Q(out_3));  // open: Qn, preset, en, reset
  J_K_Flip_Flop #(.trigger("falling")) j_k_ff_3 (
    .J(out_3), .clk(clock_1_out), .K(not_3_out), .Q(out_4));  // open: Qn, preset, en, reset
  not not_3 (not_3_out, out_3);
  not not_4 (not_4_out, out_4);
  J_K_Flip_Flop #(.trigger("falling")) j_k_ff_4 (
    .J(out_4), .clk(clock_1_out), .K(not_4_out), .Q(out_5));  // open: Qn, preset, en, reset
endmodule
