// Logisim project S2_b_AULA.circ as structural Verilog: 1 circuit, main circuit main
module main (
  input  F,
  input  G,
  input  H,
  output S
);

  wire and_1_out, and_2_out, and_3_out, not_1_out, not_2_out, not_3_out, not_4_out;

  not not_1 (not_1_out, F);
  not not_2 (not_2_out, G);
  not not_3 (not_3_out, F);
  not not_4 (not_4_out, H);
  and and_1 (and_1_out, not_1_out, not_2_out);
  and and_2 (and_2_out, not_3_out, not_4_out);
  and and_3 (and_3_out, F, G, H);
  or or_1 (S, and_1_out, and_2_out, and_3_out);
endmodule
