// Logisim project SERIE-SERIE COM FF TIPO D 4 BITS.circ as structural Verilog: 1 circuit, main circuit main
module main (
  input  ENTRADA,
  output S
);

  wire clock_1_out, d_ff_2_q, d_ff_3_q, d_ff_4_q;

  D_Flip_Flop d_ff_1 (.clk(clock_1_out), .D(d_ff_2_q), .Q(S));  // open: Qn, preset, en, reset
  D_Flip_Flop d_ff_2 (.clk(clock_1_out), .D(d_ff_3_q), .Q(d_ff_2_q));  // open: Qn, preset, en, reset
  D_Flip_Flop d_ff_3 (.clk(clock_1_out), .D(d_ff_4_q), .Q(d_ff_3_q));  // open: Qn, preset, en, reset
  D_Flip_Flop d_ff_4 (.clk(clock_1_out), .D(ENTRADA), .Q(d_ff_4_q));  // open: Qn, preset, en, reset
  Clock clock_1 (.out(clock_1_out));
endmodule
