// Logisim project SOMADOR COM SUBTRATOR.circ as structural Verilog: 1 circuit, main circuit main
module main (
  input  E0,
  input  E1,
  output S,
  output BO,
  output C0
);

  wire and_1_out, and_2_out, not_1_out, not_2_out, not_3_out;

  not not_1 (not_1_out, E0);
  and and_1 (and_1_out, not_1_out, E1);
  and and_2 (and_2_out, E0, not_2_out);
  not not_2 (not_2_out, E1);
  and and_3 (BO, E1, not_3_out);
  not not_3 (not_3_out, E0);
  or or_1 (S, and_1_out, and_2_out);
  xor xor_1 (C0, E1, BO);
endmodule
