// Logisim project SOMADOR DE REGISTRADORES.circ as structural Verilog: 1 circuit, main circuit main
module main (
);

  wire adder_1_cout, adder_1_out, clock_1_out, d_ff_1_q, d_ff_2_q, d_ff_3_q, d_ff_4_q, d_ff_5_q;

  Clock clock_1 (.out(clock_1_out));
  D_Flip_Flop d_ff_1 (.clk(clock_1_out), .D(adder_1_out), .Q(d_ff_1_q));  // open: Qn, preset, en, reset
  D_Flip_Flop d_ff_2 (.D(d_ff_1_q), .Q(d_ff_2_q));  // open: clk, Qn, preset, en, reset
  D_Flip_Flop d_ff_3 (.clk(clock_1_out), .D(d_ff_4_q), .Q(d_ff_3_q));  // open: Qn, preset, en, reset
  D_Flip_Flop d_ff_4 (.clk(clock_1_out), .D(d_ff_3_q), .Q(d_ff_4_q));  // open: Qn, preset, en, reset
  D_Flip_Flop d_ff_5 (.clk(clock_1_out), .D(adder_1_cout), .Q(d_ff_5_q));  // open: Qn, preset, en, reset
  Adder #(.width(1)) adder_1 (.a(d_ff_2_q), .b(d_ff_4_q), .out(adder_1_out), .cin(d_ff_5_q), .cout(adder_1_cout));
endmodule
