// Logisim project SOMADOR4BITS.circ as structural Verilog: 1 circuit, main circuit main
module main (
  input  [3:0] A,
  input  [3:0] B,
  output [3:0] S,
  output BO
);

  Subtractor #(.width(4)) subtractor_1 (.a(A), .b(B), .out(S), .bout(BO));  // open: bin
endmodule
