// Logisim project demux de 16 com 4 e 8 com 4.circ as structural Verilog: 1 circuit, main circuit main
module main (
  input  in_1,
  input  [1:0] in_2,
  input  [1:0] in_3,
  input  in_4,
  input  [1:0] in_5,
  input  in_6,
  output s0,
  output s1,
  output s2,
  output s3,
  output s4,
  output s5,
  output s6,
  output s7,
  output s8,
  output s9,
  output s10,
  output s11,
  output s12,
  output s13,
  output s14,
  output s15,
  output out_23,
  output out_24,
  output out_25,
  output out_26,
  output out_27,
  output out_28,
  output out_29,
  output out_30
);

  wire demultiplexer_1_out0, demultiplexer_1_out1, demultiplexer_1_out2, demultiplexer_1_out3,
       demultiplexer_2_out0, demultiplexer_2_out1, demultiplexer_2_out2, demultiplexer_2_out3;

  Demultiplexer #(.select(2), .enable("false")) demultiplexer_1 (
    .out0(demultiplexer_1_out0), .out1(demultiplexer_1_out1), .out2(demultiplexer_1_out2),
    .out3(demultiplexer_1_out3), .in(in_1), .sel(in_2));
  Demultiplexer #(.select(2), .enable("false")) demultiplexer_2 (
    .out0(demultiplexer_2_out0), .out1(demultiplexer_2_out1), .out2(demultiplexer_2_out2),
    .out3(demultiplexer_2_out3), .in(in_4), .sel(in_5));
  Demultiplexer #(.select(2), .enable("false")) demultiplexer_3 (
    .out0(s0), .out1(s1), .out2(s2), .out3(s3), .in(demultiplexer_1_out0), .sel(in_3));
  Demultiplexer #(.select(2), .enable("false")) demultiplexer_4 (
    .out0(s4), .out1(s5), .out2(s6), .out3(s7), .in(demultiplexer_1_out1), .sel(in_3));
  Demultiplexer #(.select(2), .enable("false")) demultiplexer_5 (
    .out0(s8), .out1(s9), .out2(s10), .out3(s11), .in(demultiplexer_1_out2), .sel(in_3));
  Demultiplexer #(.select(2), .enable("false")) demultiplexer_6 (
    .out0(s12), .out1(s13), .out2(s14), .out3(s15), .in(demultiplexer_1_out3), .sel(in_3));
  Demultiplexer #(.enable("false")) demultiplexer_7 (
    .out0(out_23), .out1(out_24), .in(demultiplexer_2_out0), .sel(in_6));
  Demultiplexer #(.enable("false")) demultiplexer_8 (
    .out0(out_25), .out1(out_26), .in(demultiplexer_2_out1), .sel(in_6));
  Demultiplexer #(.enable("false")) demultiplexer_9 (
    .out0(out_27), .out1(out_28), .in(demultiplexer_2_out2), .sel(in_6));
  Demultiplexer #(.enable("false")) demultiplexer_10 (
    .out0(out_29), .out1(out_30), .in(demultiplexer_2_out3), .sel(in_6));

  // Notes on the sheet:
  //   Obter o circuito de um DEMUX de 8 canais utilizando apenas DEMUX de 4 canais.
endmodule
