// Logisim project ex4-lista4-completo.circ as structural Verilog: 1 circuit, main circuit main
module main (
  input  in_1,
  input  in_2,
  input  in_3,
  input  in_4,
  input  in_5,
  input  in_6,
  input  in_7,
  input  in_8,
  output out_9,
  output out_10,
  output out_11,
  output out_12,
  output out_13,
  output out_14
);

  wire and_1_out, and_2_out, and_3_out, and_4_out, clock_1_out, clock_2_out, clock_3_out, j_k_ff_1_qn,
       j_k_ff_2_q, j_k_ff_2_qn, j_k_ff_4_q, j_k_ff_4_qn, j_k_ff_5_q, j_k_ff_5_qn, j_k_ff_6_qn, j_k_ff_7_q,
       j_k_ff_7_qn, j_k_ff_8_q, j_k_ff_8_qn, j_k_ff_9_qn, j_k_ff_12_q, j_k_ff_12_qn, not_1_out, not_2_out,
       not_3_out, not_4_out;

  not not_1 (not_1_out, in_1);
  Clock clock_1 (.out(clock_1_out));
  not not_2 (not_2_out, in_2);
  Clock clock_2 (.out(clock_2_out));
  not not_3 (not_3_out, in_3);
  Clock clock_3 (.out(clock_3_out));
  J_K_Flip_Flop j_k_ff_1 (
    .J(in_1), .clk(clock_1_out), .K(not_1_out), .Q(out_10), .Qn(j_k_ff_1_qn));  // open: preset, en, reset
  J_K_Flip_Flop j_k_ff_2 (
    .J(in_2), .clk(clock_2_out), .K(not_2_out), .Q(j_k_ff_2_q), .Qn(j_k_ff_2_qn), .preset(and_1_out));  // open: en, reset
  and and_1 (and_1_out, in_4, not_3_out);
  J_K_Flip_Flop j_k_ff_3 (
    .J(j_k_ff_5_q), .clk(clock_3_out), .K(j_k_ff_5_qn), .Q(out_14));  // open: Qn, preset, en, reset
  J_K_Flip_Flop j_k_ff_4 (
    .J(j_k_ff_2_q), .clk(clock_2_out), .K(j_k_ff_2_qn), .Q(j_k_ff_4_q), .Qn(j_k_ff_4_qn), .preset(and_2_out));  // open: en, reset
  and and_2 (and_2_out, in_5, not_3_out);
  J_K_Flip_Flop j_k_ff_5 (
    .J(j_k_ff_8_q), .clk(clock_3_out), .K(j_k_ff_8_qn), .Q(j_k_ff_5_q), .Qn(j_k_ff_5_qn));  // open: preset, en, reset
  J_K_Flip_Flop j_k_ff_6 (
    .J(out_10), .clk(clock_1_out), .K(j_k_ff_1_qn), .Q(out_11), .Qn(j_k_ff_6_qn));  // open: preset, en, reset
  J_K_Flip_Flop j_k_ff_7 (
    .J(j_k_ff_4_q), .clk(clock_2_out), .K(j_k_ff_4_qn), .Q(j_k_ff_7_q), .Qn(j_k_ff_7_qn), .preset(and_3_out));  // open: en, reset
  and and_3 (and_3_out, in_6, not_3_out);
  and and_4 (and_4_out, in_7, not_3_out);
  J_K_Flip_Flop j_k_ff_8 (
    .J(j_k_ff_12_q), .clk(clock_3_out), .K(j_k_ff_12_qn), .Q(j_k_ff_8_q), .Qn(j_k_ff_8_qn));  // open: preset, en, reset
  J_K_Flip_Flop j_k_ff_9 (
    .J(out_11), .clk(clock_1_out), .K(j_k_ff_6_qn), .Q(out_9), .Qn(j_k_ff_9_qn));  // open: preset, en, reset
  J_K_Flip_Flop j_k_ff_10 (
    .J(j_k_ff_7_q), .clk(clock_2_out), .K(j_k_ff_7_qn), .Q(out_13), .preset(and_4_out));  // open: Qn, en, reset
  not not_4 (not_4_out, in_8);
  J_K_Flip_Flop j_k_ff_11 (.J(out_9), .clk(clock_1_out), .K(j_k_ff_9_qn), .Q(out_12));  // open: Qn, preset, en, reset
  J_K_Flip_Flop j_k_ff_12 (
    .J(in_8), .clk(clock_3_out), .K(not_4_out), .Q(j_k_ff_12_q), .Qn(j_k_ff_12_qn));  // open: preset, en, reset
endmodule
