// Logisim project ex5-lista4.circ as structural Verilog: 1 circuit, main circuit main
module main (
  output a,
  output b,
  output c
);

  wire and_1_out, and_2_out, clock_1_out, d_ff_2_q, d_ff_3_q, not_1_out, not_2_out;

  Clock clock_1 (.out(clock_1_out));
  D_Flip_Flop d_ff_1 (.clk(clock_1_out), .D(a), .Q(a));  // open: Qn, preset, en, reset
  not not_1 (not_1_out, d_ff_2_q);
  not not_2 (not_2_out, d_ff_3_q);
  not not_3 (c, d_ff_3_q);
  D_Flip_Flop d_ff_2 (.clk(clock_1_out), .D(b), .Q(d_ff_2_q));  // open: Qn, preset, en, reset
  and and_1 (and_1_out, not_1_out, not_2_out);
  and and_2 (and_2_out, d_ff_2_q, d_ff_3_q);
  or or_1 (b, and_1_out, and_2_out);
  D_Flip_Flop d_ff_3 (.clk(clock_1_out), .D(c), .Q(d_ff_3_q));  // open: Qn, preset, en, reset
endmodule
