// Logisim project memória ram 2kX16.circ as structural Verilog: 1 circuit, main circuit main
module main (
  input  [10:0] \Posição_Memória ,
  input  [15:0] Entrada,
  input  Sel,
  input  R_W,
  input  Clear,
  output [15:0] \Saída 
);

  wire CK_out;

  Clock CK (.out(CK_out));
  RAM #(.addrWidth(11), .dataWidth(16), .bus("separate")) ram_1 (
    .addr(\Posição_Memória ), .din(Entrada), .data(\Saída ), .sel(Sel), .clk(CK_out), .ld(R_W), .clr(Clear));  // open: str
endmodule
