// Logisim project memória ram.circ as structural Verilog: 1 circuit, main circuit main
module main (
  input  [7:0] \Posição_Memória ,
  input  [7:0] Entrada,
  input  Sel,
  input  R_W,
  input  Clear,
  output [7:0] \Saída 
);

  wire CK_out;

  Clock CK (.out(CK_out));
  RAM ram_1 (.addr(\Posição_Memória ), .data(Entrada), .sel(Sel), .clk(CK_out), .ld(R_W), .clr(Clear));

  assign \Saída  = Entrada;
endmodule
