// Logisim project mux2CANAIS.circ as structural Verilog: 1 circuit, main circuit main
module main (
  input  E0,
  input  E1,
  input  A,
  output S
);

  Multiplexer #(.enable("false")) multiplexer_1 (.in0(E0), .in1(E1), .out(S), .sel(A));

  // Notes on the sheet:
  //   MUX de 2 canais
endmodule
